// Logisim project Tarea1_Circ_Comb.circ as structural Verilog: 6 circuits, main circuit main
module main (
  input  B3,
  input  B2,
  input  B1,
  input  B0,
  input  EL,
  input  EF,
  input  ER,
  input  CL,
  input  CF,
  input  CR,
  output Left,
  output Front,
  output Right
);

  wire and_1_out, and_2_out, and_3_out, and_4_out, and_5_out, and_6_out, and_7_out, and_8_out, and_9_out,
       and_10_out, and_11_out, and_12_out, not_1_out, not_2_out, not_3_out, not_4_out, not_5_out, not_6_out,
       not_7_out, not_8_out, not_9_out, not_10_out, not_11_out, not_12_out, not_13_out, not_14_out,
       not_15_out, not_16_out, not_17_out, not_18_out, not_19_out, not_20_out, not_21_out, not_22_out,
       not_23_out, not_24_out;

  not not_1 (not_1_out, B3);
  not not_2 (not_2_out, B2);
  and and_1 (and_1_out, not_1_out, not_2_out);
  not not_3 (not_3_out, EL);
  not not_4 (not_4_out, CF);
  not not_5 (not_5_out, CR);
  not not_6 (not_6_out, EL);
  not not_7 (not_7_out, CF);
  not not_8 (not_8_out, EL);
  not not_9 (not_9_out, ER);
  not not_10 (not_10_out, CF);
  not not_11 (not_11_out, CR);
  not not_12 (not_12_out, EL);
  not not_13 (not_13_out, and_1_out);
  not not_14 (not_14_out, EL);
  not not_15 (not_15_out, CR);
  not not_16 (not_16_out, EL);
  not not_17 (not_17_out, EF);
  not not_18 (not_18_out, and_1_out);
  not not_19 (not_19_out, EF);
  not not_20 (not_20_out, ER);
  not not_21 (not_21_out, CF);
  not not_22 (not_22_out, ER);
  not not_23 (not_23_out, ER);
  not not_24 (not_24_out, and_1_out);
  and and_2 (and_2_out, not_3_out, CL, not_4_out, not_5_out, and_1_out);
  and and_3 (and_3_out, not_6_out, ER, CL, not_7_out, and_1_out);
  and and_4 (and_4_out, not_8_out, EF, not_9_out, not_10_out, not_11_out);
  and and_5 (and_5_out, not_12_out, EF, not_13_out);
  and and_6 (and_6_out, not_14_out, EF, CL, not_15_out);
  and and_7 (and_7_out, not_16_out, EF, ER, CL);
  and and_8 (and_8_out, not_17_out, not_18_out);
  and and_9 (and_9_out, not_19_out, CF);
  and and_10 (and_10_out, not_20_out, not_21_out, CR, and_1_out);
  and and_11 (and_11_out, EF, not_22_out, CR, and_1_out);
  and and_12 (and_12_out, EL, EF, not_23_out, not_24_out);
  or or_1 (Left, and_2_out, and_3_out, and_4_out, and_5_out, and_6_out, and_7_out);
  or or_2 (Front, and_8_out, and_9_out);
  or or_3 (Right, and_10_out, and_11_out, and_12_out);
endmodule

module Movimiento_Enemigos (
  input  EL,
  input  EF,
  input  ER,
  output L,
  output F,
  output R
);

  wire and_1_out, not_1_out, not_3_out;

  not not_1 (not_1_out, EL);
  not not_2 (F, EF);
  and and_1 (and_1_out, EL, EF);
  not not_3 (not_3_out, ER);
  and and_2 (L, not_1_out, EF);
  and and_3 (R, and_1_out, not_3_out);
endmodule

module Movimiento_Energia (
  input  CL,
  input  CF,
  input  CR,
  output L,
  output F,
  output R
);

  wire and_1_out, not_1_out, not_2_out, not_3_out;

  not not_1 (not_1_out, CF);
  not not_2 (not_2_out, CF);
  and and_1 (and_1_out, CL, not_1_out);
  not not_3 (not_3_out, CR);
  and and_2 (R, not_2_out, CR);
  and and_3 (L, and_1_out, not_3_out);

  assign F = CF;
endmodule

module Energia (
  input  E3,
  input  E2,
  input  E1,
  input  E0,
  output y
);

  wire not_1_out, not_2_out;

  not not_1 (not_1_out, E3);
  not not_2 (not_2_out, E2);
  and and_1 (y, not_1_out, not_2_out);
endmodule

module Comparacao (
  input  EntradaEnem,
  input  EntradaCarga,
  input  Energia,
  output Y
);

  wire and_1_out, and_2_out, not_1_out;

  and and_1 (and_1_out, EntradaCarga, Energia);
  and and_2 (and_2_out, EntradaEnem, not_1_out);
  not not_1 (not_1_out, Energia);
  or or_1 (Y, and_1_out, and_2_out);
endmodule

module test (
  input  B,
  input  EL,
  input  EF,
  input  ER,
  input  CL,
  input  CF,
  input  CR,
  output Left,
  output Front,
  output Right
);

  wire and_1_out, and_2_out, and_3_out, and_4_out, and_5_out, and_6_out, and_7_out, and_8_out, and_9_out,
       and_10_out, and_11_out, not_1_out, not_2_out, not_3_out, not_4_out, not_5_out, not_6_out, not_7_out,
       not_8_out, not_9_out, not_10_out, not_11_out, not_12_out, not_13_out, not_14_out, not_15_out,
       not_16_out, not_17_out, not_18_out, not_19_out, not_20_out, not_21_out, not_22_out;

  not not_1 (not_1_out, EL);
  not not_2 (not_2_out, CF);
  not not_3 (not_3_out, CR);
  not not_4 (not_4_out, EL);
  not not_5 (not_5_out, CF);
  not not_6 (not_6_out, EL);
  not not_7 (not_7_out, ER);
  not not_8 (not_8_out, CF);
  not not_9 (not_9_out, CR);
  not not_10 (not_10_out, EL);
  not not_11 (not_11_out, B);
  not not_12 (not_12_out, EL);
  not not_13 (not_13_out, CR);
  not not_14 (not_14_out, EL);
  not not_15 (not_15_out, EF);
  not not_16 (not_16_out, B);
  not not_17 (not_17_out, EF);
  not not_18 (not_18_out, ER);
  not not_19 (not_19_out, CF);
  not not_20 (not_20_out, ER);
  not not_21 (not_21_out, ER);
  not not_22 (not_22_out, B);
  and and_1 (and_1_out, not_1_out, CL, not_2_out, not_3_out, B);
  and and_2 (and_2_out, not_4_out, ER, CL, not_5_out, B);
  and and_3 (and_3_out, not_6_out, EF, not_7_out, not_8_out, not_9_out);
  and and_4 (and_4_out, not_10_out, EF, not_11_out);
  and and_5 (and_5_out, not_12_out, EF, CL, not_13_out);
  and and_6 (and_6_out, not_14_out, EF, ER, CL);
  and and_7 (and_7_out, not_15_out, not_16_out);
  and and_8 (and_8_out, not_17_out, CF);
  and and_9 (and_9_out, not_18_out, not_19_out, CR, B);
  and and_10 (and_10_out, EF, not_20_out, CR, B);
  and and_11 (and_11_out, EL, EF, not_21_out, not_22_out);
  or or_1 (Left, and_1_out, and_2_out, and_3_out, and_4_out, and_5_out, and_6_out);
  or or_2 (Front, and_7_out, and_8_out);
  or or_3 (Right, and_9_out, and_10_out, and_11_out);
endmodule
